// Digital circuit main.dig as structural Verilog
module main (
  input  Clock,
  output [15:0] I,
  output [5:0] FUNCT
);

  wire AC, ALU_SRC, d_ff_1_q, d_ff_2_q, id_ex_1_o_alus, MEM_TO_REG, MR, Reg_dest, RW, ula_1_p6, undriven,
       Write_MEM;
  wire [1:0] AO, id_ex_1_o_ao;
  wire [4:0] multiplexer_1_out;
  wire [5:0] OPCODE;
  wire [23:0] ula_1_p5;
  wire [25:16] if_id_1_out;
  wire [31:0] _32x32_1_r_d1, _32x32_1_r_d2, add_1_s, bitextender_1_out, id_ex_1_o_r1, id_ex_1_o_r2,
       id_ex_1_out_s32, instruction_mem_1__32b__out, memory_24x32_1_d, multiplexer_2_out, pc_1_pc_out, R31,
       WB;
  wire [31:24] ula_1_p5_2;

  PC pc_1 (.Clok(Clock), .PC_IN(add_1_s), .PC_OUT(pc_1_pc_out));
  Add #(.Bits(32)) add_1 (.a(pc_1_pc_out), .b(32'h4), .c_i(1'b0), .s(add_1_s));  // open: c_o
  instruction_mem instruction_mem_1 (
    ._32b__ADDR(pc_1_pc_out), ._1b__Enable(Clock), ._32b__Out(instruction_mem_1__32b__out));
  IF_ID if_id_1 (.In(instruction_mem_1__32b__out), .Clk(Clock), .Out({OPCODE, if_id_1_out, I[15:6], FUNCT}));
  Control control_1 (
    .RgD(Reg_dest), .AluS(ALU_SRC), .MTR(MEM_TO_REG), .RW(RW), .MR(MR), .MW(Write_MEM), .AO_1(AO[0]),
    .AO_0(AO[1]), .Clk(Clock), .Op(OPCODE));  // open: B, J, APC
  Multiplexer #(.Bits(5)) multiplexer_1 (
    .sel(Reg_dest), .in_0(if_id_1_out[20:16]), .in_1(I[15:11]), .out(multiplexer_1_out));
  _32x32 _32x32_1 (
    ._32_W_d(WB), ._5__R_reg1(if_id_1_out[25:21]), ._5__R_reg2(if_id_1_out[20:16]),
    ._5b__A_set(multiplexer_1_out), .Clk(Clock), ._1__W_e(d_ff_2_q), .R_d1(_32x32_1_r_d1),
    .R_d2(_32x32_1_r_d2), .R31(R31));
  D_FF d_ff_1 (.D(RW), .C(~Clock), .Q(d_ff_1_q));  // open: nQ
  D_FF d_ff_2 (.D(d_ff_1_q), .C(Clock), .Q(d_ff_2_q));  // open: nQ
  BitExtender #(.inputBits(16), .outputBits(32)) bitextender_1 (.in({I[15:6], FUNCT}), .out(bitextender_1_out));
  ID_EX id_ex_1 (
    .MR(MR), .MW(Write_MEM), .MTR(MEM_TO_REG), .AluS(ALU_SRC), .AO(AO), .R_1(_32x32_1_r_d1),
    .R_2(_32x32_1_r_d2), .S_32(bitextender_1_out), .Clk(Clock), .O_AluS(id_ex_1_o_alus), .O_AO(id_ex_1_o_ao),
    .O_R1(id_ex_1_o_r1), .O_R2(id_ex_1_o_r2), .Out_S32(id_ex_1_out_s32));  // open: RgD, O_MR, O_MW, O_MTR, O_RgD
  Seven_Seg_Hex seven_seg_hex_1 (.d(R31[19:16]), .dp(1'b0));
  Seven_Seg_Hex seven_seg_hex_2 (.d(R31[15:12]), .dp(1'b0));
  Multiplexer #(.Bits(32)) multiplexer_2 (
    .sel(id_ex_1_o_alus), .in_0(id_ex_1_o_r2), .in_1(id_ex_1_out_s32), .out(multiplexer_2_out));
  // ALU_Control alu_control_1: pin names not known; wires that end beside it: if_id_1_out[20:16], I[15:11], id_ex_1_o_ao[0], id_ex_1_o_ao[1], FUNCT, AC
  Seven_Seg_Hex seven_seg_hex_3 (.d(R31[11:8]), .dp(1'b0));
  Seven_Seg_Hex seven_seg_hex_4 (.d(R31[7:4]), .dp(1'b0));
  // ula ula_1: pin names not known; wires that end beside it: AC, id_ex_1_o_r1, multiplexer_2_out, {6{1'b0}}, {ula_1_p5_2, ula_1_p5}, ula_1_p6
  Seven_Seg_Hex seven_seg_hex_5 (.d(R31[3:0]), .dp(1'b0));
  memory_24x32 memory_24x32_1 (
    .A(ula_1_p5), .Data_in(id_ex_1_o_r2), .MW(ula_1_p6), .Clk(Clock), .MR(undriven), .D(memory_24x32_1_d));
  Multiplexer #(.Bits(32)) multiplexer_3 (
    .in_0({ula_1_p5_2, ula_1_p5}), .in_1(memory_24x32_1_d), .out(WB));  // open: sel

  assign I[5:0] = FUNCT;

  // Notes on the sheet:
  //   I: Imediato
  //   Instrução [15-0]
  //   Instrução [20-16]
  //   Instrução [15-11]
  //   AluOP
endmodule
